# Fritzing sketch Tempera-Circuit-Layout (saved by Fritzing 0.9.3b)
breadboards: 1

parts:
  Arduino_Nano_33_BLE = Arduino Nano (Rev3.0)
  S1 = Pushbutton [package="[THT]"]
  S2 = Pushbutton [package="[THT]"]
  S3 = Pushbutton [package="[THT]"]
  R1 = Resistor [tolerance=±5% resistance=220 package="0402 [SMD]"]
  R2 = Resistor [tolerance=±5% resistance=220 package="0402 [SMD]"]
  R3 = Resistor [tolerance=±5% resistance=220 package="0402 [SMD]"]
  Bauteil1 = Adafruit BME680 [part_number="Adafruit #3660"]
  LED1 = RGB LED (com. cathode, rbg) [package="5 mm [THT]"]
  S4 = Pushbutton [package="[THT]"]
  Q1 = LTR-301 [package=ltr-301]
  R4 = Resistor [tolerance=±5% resistance=2.2k package="0805 [SMD]"]

nets (from the schematic view):
  GND: Arduino_Nano_33_BLE.GND, S1.Pin_3, S1.Pin_4, S2.Pin_3, S2.Pin_4, S3.Pin_3, S3.Pin_4, Bauteil1.GND, LED1.common_cathode, S4.Pin_3, S4.Pin_4, R4.Pin_1
  N1: Arduino_Nano_33_BLE.D2, S1.Pin_1, S1.Pin_2
  N2: Arduino_Nano_33_BLE.D3, S2.Pin_1, S2.Pin_2
  N3: Arduino_Nano_33_BLE.D4, S3.Pin_1, S3.Pin_2
  N4: Arduino_Nano_33_BLE.D5, S4.Pin_1, S4.Pin_2
  N5: Arduino_Nano_33_BLE.A7, Q1.E, R4.Pin_0
  N6: Arduino_Nano_33_BLE.A5, Bauteil1.SCK/SCL
  N7: Arduino_Nano_33_BLE.A4, Bauteil1.SDI/SDA
  N8: Arduino_Nano_33_BLE.A2, R2.Pin_0
  N9: Arduino_Nano_33_BLE.A1, R3.Pin_0
  N10: Arduino_Nano_33_BLE.A0, R1.Pin_0
  3V3: Arduino_Nano_33_BLE.3V3, Bauteil1.VCC, Q1.C
  N11: R1.Pin_1, LED1.red_anode
  N12: R2.Pin_1, LED1.blue_anode
  N13: R3.Pin_1, LED1.green_anode
